# Fritzing sketch Sketch_18650_TB6612 (saved by Fritzing 0.9.5d)

parts:
  ESP32_-_Back1 = ESP32 - CAM
  M1 = DC Motor
  Vertical_Servo = Basic Servo
  Part2 = Motor Driver 1A Dual TB6612FNG
  5V_Step_UP = Mini-360 DC-DC Buck converter [package=THT]
  Horizontal_Servo = Basic Servo
  5V_Step_UP_2 = Mini-360 DC-DC Buck converter [package=THT]
  6-12V_Step_UP = Mini-360 DC-DC Buck converter [package=THT]
  3_7V = Parallel 18650 battery
  C1 = Capacitor [package=cap-pth-small2]
  C2 = Capacitor [package=cap-pth-small2]
  470uF = Capacitor Polarized [package=panasonic_e]
  TP4056 = TP4056 [chip_label=TP4056 package="DIP (Dual Inline) [THT]"]
  S1 = Toggle Switch spst [package=THT]
  M2 = DC Motor
  470uF_2 = Capacitor Polarized [package=panasonic_e]

nets:
  N1: ESP32_-_Back1.GPIO2, Part2.BIN2
  N2: ESP32_-_Back1.GPIO14, Part2.BIN1
  N3: ESP32_-_Back1.GPIO15, Part2.AIN1
  N4: ESP32_-_Back1.GPIO13, Part2.AIN2
  N5: ESP32_-_Back1.GPIO12, Horizontal_Servo.pulse
  GND: ESP32_-_Back1.GND, Part2.GND, 5V_Step_UP.OUT-, 6-12V_Step_UP.OUT-, 470uF_2.-
  N6: ESP32_-_Back1.5V, 5V_Step_UP.OUT+, 470uF.+
  N7: ESP32_-_Back1.GPIO3_/_RX, Vertical_Servo.pulse
  N8: M1.pin_1, Part2.B01, C1.1
  N9: M1.pin_2, Part2.B02, C1.2
  GND_2: Vertical_Servo.gnd, Horizontal_Servo.gnd, 5V_Step_UP_2.OUT-
  VCC: Vertical_Servo.vcc, Horizontal_Servo.vcc, 5V_Step_UP_2.OUT+
  N10: Part2.A02, C2.1, M2.pin_1
  N11: Part2.A01, C2.2, M2.pin_2
  N12: Part2.VCC, Part2.PWMA
  N13: Part2.VM, 6-12V_Step_UP.OUT+, 470uF_2.+
  N14: Part2.STBY, Part2.PWMB
  N15: 5V_Step_UP_2.IN-, TP4056.pin6
  N16: 6-12V_Step_UP.IN+, TP4056.pin3
  N17: 3_7V.+, S1.L1
  N18: TP4056.pin4, S1.COM

custom parts:
  ESP32 - CAM: The ESP32-CAM has a very competitive small-size camera module that can operate independently as a minimum system with a footprint of only 27*40.5*4.5mm and a deep sleep current of up to 6mA.
  Mini-360 DC-DC Buck converter: Mini-360 DC-DC Buck converter. Tiny buck step down voltage converter, input voltage 4.75 to 23V output 1 to 17V adjustable. Available from ebay and the like.
  Parallel 18650 battery: 2x 18650 battery pack (3.7 Volts)
  TP4056: A DIP stand-in part for whatever IC you want. With 6 pins on a 300mil dual inline package (DIP) footprint.
  Toggle Switch spst: Toggle Switch single pole single throw
