# Fritzing sketch Sketch_9V_2PIN_DRV (saved by Fritzing 0.9.5d)

parts:
  ESP32_-_Back1 = ESP32 - CAM
  M1 = DC Motor
  Vertical_Servo = Basic Servo
  Horizontal_Servo = Basic Servo
  6-12V_Step_up_OR_down = Mini-360 DC-DC Buck converter [package=THT]
  C1 = Capacitor [package=cap-pth-small2]
  C2 = Capacitor [package=cap-pth-small2]
  470uF = Capacitor Polarized [package=panasonic_e]
  S1 = Toggle Switch spst [package=THT]
  M2 = DC Motor
  S2 = H-Bridge with L298N
  470uF_2 = Capacitor Polarized [package=panasonic_e]
  BAT1 = BC9VPC [package=bc9vpc]
  5V_Step_Down = MP1584EN Power Regulator Board [part_number=MP1584EN]
  5V_Step_Down_2 = MP1584EN Power Regulator Board [part_number=MP1584EN]

nets:
  N1: ESP32_-_Back1.GPIO2, S2.IN1
  N2: ESP32_-_Back1.GPIO14, S2.IN2
  N3: ESP32_-_Back1.GPIO15, S2.IN3
  N4: ESP32_-_Back1.GPIO13, S2.IN4
  N5: ESP32_-_Back1.GPIO12, Horizontal_Servo.pulse
  N6: ESP32_-_Back1.GND, 5V_Step_Down.OUT_-
  N7: ESP32_-_Back1.5V, 470uF.+, 5V_Step_Down.OUT_+
  N8: ESP32_-_Back1.GPIO3_/_RX, Vertical_Servo.pulse
  N9: M1.pin_1, C1.1, S2.M1-02
  N10: M1.pin_2, C1.2, S2.M1-01
  N11: Vertical_Servo.gnd, 5V_Step_Down_2.OUT_-#14
  N12: Vertical_Servo.vcc, 5V_Step_Down_2.OUT_+#16
  N13: Horizontal_Servo.gnd, 5V_Step_Down_2.OUT_-#13
  N14: Horizontal_Servo.vcc, 5V_Step_Down_2.OUT_+#15
  N15: 6-12V_Step_up_OR_down.IN-, BAT1.V-, 5V_Step_Down.IN_-
  N16: 6-12V_Step_up_OR_down.IN+, S1.COM, 5V_Step_Down.IN_+, 5V_Step_Down_2.IN_+
  N17: 6-12V_Step_up_OR_down.OUT+, S2.12V, 470uF_2.+
  N18: 6-12V_Step_up_OR_down.OUT-, S2.GND, 470uF_2.-
  N19: C2.1, M2.pin_1, S2.M2-02
  N20: C2.2, M2.pin_2, S2.M2-01
  N21: S1.L1, BAT1.V+
  N22: S2.ENA, S2.ENA-5V
  N23: S2.ENB, S2.ENB-5V

custom parts:
  ESP32 - CAM: The ESP32-CAM has a very competitive small-size camera module that can operate independently as a minimum system with a footprint of only 27*40.5*4.5mm and a deep sleep current of up to 6mA.
  Mini-360 DC-DC Buck converter: Mini-360 DC-DC Buck converter. Tiny buck step down voltage converter, input voltage 4.75 to 23V output 1 to 17V adjustable. Available from ebay and the like.
  Toggle Switch spst: Toggle Switch single pole single throw
  H-Bridge with L298N: h-bridge
  MP1584EN Power Regulator Board: The MP1584EN is a high frequency step-down switching regulator. The input voltage range is 4.5V to 28V. The output voltage is set by the board's potentiometer.
