# Fritzing sketch Sketch_TP100_12V_2PIN_DRV (saved by Fritzing 0.9.5d)

parts:
  ESP32_-_Back1 = ESP32 - CAM
  M1 = DC Motor
  Vertical_Servo = Basic Servo
  Horizontal_Servo = Basic Servo
  C1 = Capacitor [package=cap-pth-small2]
  C2 = Capacitor [package=cap-pth-small2]
  S1 = Toggle Switch spst [package=THT]
  M2 = DC Motor
  S2 = H-Bridge with L298N
  470uF = Capacitor Polarized [package=panasonic_e]
  part = MP1584EN Power Regulator Board [part_number="5V Step down"]
  part_2 = Lithium Ion Polymer Battery 3.7v 2000mAh [part_number=12V]
  470uF_2 = Capacitor Polarized [package=panasonic_e]

nets:
  N1: ESP32_-_Back1.GPIO2, S2.IN1
  N2: ESP32_-_Back1.GPIO14, S2.IN2
  N3: ESP32_-_Back1.GPIO15, S2.IN3
  N4: ESP32_-_Back1.GPIO13, S2.IN4
  N5: ESP32_-_Back1.GPIO12, Horizontal_Servo.pulse
  GND: ESP32_-_Back1.GND, Vertical_Servo.gnd, Horizontal_Servo.gnd, part.OUT_-, 470uF_2.-
  VCC: ESP32_-_Back1.5V, Vertical_Servo.vcc, Horizontal_Servo.vcc, part.OUT_+, 470uF_2.+
  N6: ESP32_-_Back1.GPIO3_/_RX, Vertical_Servo.pulse
  N7: M1.pin_1, C1.1, S2.M1-02
  N8: M1.pin_2, C1.2, S2.M1-01
  N9: C2.1, M2.pin_1, S2.M2-02
  N10: C2.2, M2.pin_2, S2.M2-01
  N11: S1.L1, part_2.positive
  N12: S1.COM, S2.12V, 470uF.+, part.IN_+
  N13: S2.GND, 470uF.-, part.IN_-, part_2.negative
  N14: S2.ENA, S2.ENA-5V
  N15: S2.ENB, S2.ENB-5V

custom parts:
  ESP32 - CAM: The ESP32-CAM has a very competitive small-size camera module that can operate independently as a minimum system with a footprint of only 27*40.5*4.5mm and a deep sleep current of up to 6mA.
  Toggle Switch spst: Toggle Switch single pole single throw
  H-Bridge with L298N: h-bridge
  MP1584EN Power Regulator Board: The MP1584EN is a high frequency step-down switching regulator. The input voltage range is 4.5V to 28V. The output voltage is set by the board's potentiometer.
  Lithium Ion Polymer Battery 3.7v 2000mAh: Lithium ion polymer (also known as 'lipo' or 'lipoly') batteries are thin, light and powerful. The output ranges from 4.2V when completely charged to 3.7V. This battery has a capacity of 2000mAh. The batteries come pre-attached with a genuine 2-pin JST-PH connector as shown and include the necessary protection circuitry.
